// Logisim project mapa.circ as structural Verilog: 2 circuits, main circuit main
module main (
);

  LogicaEstados LogicaEstados ();
  _7_Segment_Display u_7_segment_display_1 ();  // open: g, f, a, b, e, d, c, dp
endmodule

module LogicaEstados (
);

  wire A_q, A_qn, AD_out, B_q, B_qn, BC_out, BCD_out, BD_BC_out, BD_out, C_q, C_qn, CD_out, clock_1_out, D_q,
       minus_A_B__C_A_out, minus_A_B_C_A_out, minus_A_B_out, minus_AB__BD_out, minus_AB_out, minus_AC_CD_out,
       minus_AC_out, minus_BD_out;

  Clock clock_1 (.out(clock_1_out));
  J_K_Flip_Flop A (.J(BD_BC_out), .clk(clock_1_out), .K(BCD_out), .Q(A_q), .Qn(A_qn));  // open: preset, en, reset
  J_K_Flip_Flop B (.J(D_q), .clk(clock_1_out), .K(minus_AC_CD_out), .Q(B_q), .Qn(B_qn));  // open: preset, en, reset
  J_K_Flip_Flop C (.J(AD_out), .clk(clock_1_out), .K(minus_AB__BD_out), .Q(C_q), .Qn(C_qn));  // open: preset, en, reset
  J_K_Flip_Flop D (
    .J(minus_A_B__C_A_out), .clk(clock_1_out), .K(minus_A_B_C_A_out), .Q(D_q));  // open: Qn, preset, en, reset
  and BC (BC_out, B_q, C_q);
  and BCD (BCD_out, B_q, C_q, D_q);
  and BD (BD_out, B_q, D_q);
  and AD (AD_out, A_q, D_q);
  and CD (CD_out, C_q, D_q);
  and minus_AC (minus_AC_out, A_qn, C_q);
  and minus_AB (minus_AB_out, A_qn, B_q);
  and minus_BD (minus_BD_out, B_qn, D_q);
  and minus_A_B (minus_A_B_out, A_qn, B_qn);
  or BD_BC (BD_BC_out, BC_out, BD_out);
  or minus_AC_CD (minus_AC_CD_out, CD_out, minus_AC_out);
  or minus_AB__BD (minus_AB__BD_out, minus_AB_out, minus_BD_out);
  or minus_A_B_C_A (minus_A_B_C_A_out, minus_A_B_out, C_q, A_q);
  or minus_A_B__C_A (minus_A_B__C_A_out, minus_A_B_out, C_qn, A_q);
endmodule
